// Logisim project 16-bit_register.circ as structural Verilog: 5 circuits, main circuit main
module main (
  input  clear,
  input  load,
  input  decrement,
  input  increment,
  input  i0,
  input  i1,
  input  i2,
  input  i3,
  input  i4,
  input  i5,
  input  i6,
  input  i7,
  input  i8,
  input  i9,
  input  i10,
  input  i11,
  input  i12,
  input  i13,
  input  i14,
  input  i15,
  output out_21,
  output out_22,
  output out_23,
  output out_24,
  output out_25,
  output out_26,
  output out_27,
  output out_28,
  output out_29,
  output out_30,
  output out_31,
  output out_32,
  output out_33,
  output out_34,
  output out_35,
  output out_36
);

  wire clk_out;

  Clock clk (.out(clk_out));
  reg_16bit reg_16bit_1 (
    .clear(clear), .load(load), .decrement(decrement), .increment(increment), .i0(i15), .i1(i14), .i2(i13),
    .i3(i12), .i4(i11), .i5(i10), .i6(i9), .i7(i8), .in_13(i7), .input9(i6), .input10(i5), .in_16(i4),
    .in_17(i3), .input13(i2), .input14(i1), .in_20(i0), .out_21(out_36), .out_22(out_35), .out_23(out_34),
    .out_24(out_33), .out_25(out_32), .out_26(out_31), .out_27(out_30), .out_28(out_29), .out_29(out_28),
    .out_30(out_27), .out_31(out_26), .out_32(out_25), .out_33(out_24), .out_34(out_23), .out_35(out_22),
    .out_36(out_21));

  // Notes on the sheet:
  //   16-bit register
endmodule

module reg_2bit (
  input  clear,
  input  load,
  input  decrement,
  input  increment,
  input  input0,
  input  input1,
  output out_7,
  output out_8,
  output out_9,
  output out_10,
  output out_11
);

  wire and_1_out, and_2_out, and_3_out, and_4_out, and_5_out, and_6_out, and_7_out, clock_1_out, j_k_ff_1_qn,
       not_1_out, not_2_out, not_3_out, not_4_out, not_5_out, or_1_out, or_2_out, or_3_out, or_4_out;

  not not_1 (not_1_out, clear);
  not not_2 (not_2_out, load);
  not not_3 (not_3_out, decrement);
  and and_1 (and_1_out, not_1_out, load);
  and and_2 (and_2_out, not_1_out, not_2_out, decrement);
  and and_3 (and_3_out, not_1_out, not_2_out, not_3_out, increment);
  not not_4 (not_4_out, input0);
  not not_5 (not_5_out, input1);
  and and_4 (and_4_out, and_1_out, input0);
  and and_5 (and_5_out, and_1_out, not_4_out);
  and and_6 (and_6_out, and_1_out, input1);
  and inc (out_10, out_7, and_3_out);
  and dec (out_11, j_k_ff_1_qn, and_2_out);
  and and_7 (and_7_out, and_1_out, not_5_out);
  or or_1 (or_1_out, and_4_out, and_2_out, and_3_out);
  or or_2 (or_2_out, clear, and_2_out, and_3_out, and_5_out);
  or or_3 (or_3_out, and_6_out, out_11, out_10);
  or or_4 (or_4_out, clear, out_10, out_11, and_7_out);
  Clock clock_1 (.out(clock_1_out));
  J_K_Flip_Flop j_k_ff_1 (
    .J(or_1_out), .clk(clock_1_out), .K(or_2_out), .Q(out_7), .Qn(j_k_ff_1_qn));  // open: preset, reset
  J_K_Flip_Flop j_k_ff_2 (.J(or_3_out), .clk(clock_1_out), .K(or_4_out), .Q(out_8), .Qn(out_9));  // open: preset, reset

  // Notes on the sheet:
  //   C
  //   L
  //   D
  //   I
  //   L.I0
  //   L.I0'
  //   L.I1
  //   L.I1'
endmodule

module reg_4bit (
  input  clear,
  input  load,
  input  decrement,
  input  i0,
  input  i1,
  input  increment,
  input  in_7,
  input  in_8,
  output out_9,
  output out_10,
  output out_11,
  output out_12,
  output out_13,
  output out_14,
  output out_15
);

  wire and_1_out, and_2_out, and_3_out, and_4_out, and_5_out, and_6_out, and_7_out, clock_1_out, dec_out,
       inc_out, j_k_ff_1_qn, not_1_out, not_2_out, not_3_out, not_4_out, not_5_out, or_1_out, or_2_out,
       or_3_out, or_4_out, reg_2bit_1_out_9, reg_2bit_1_out_10, reg_2bit_1_out_11;

  not not_1 (not_1_out, clear);
  not not_2 (not_2_out, load);
  not not_3 (not_3_out, decrement);
  and and_1 (and_1_out, not_1_out, load);
  and and_2 (and_2_out, not_1_out, not_2_out, decrement);
  and and_3 (and_3_out, not_1_out, not_2_out, not_3_out, increment);
  not not_4 (not_4_out, in_7);
  not not_5 (not_5_out, in_8);
  reg_2bit reg_2bit_1 (
    .clear(clear), .load(and_1_out), .decrement(and_2_out), .increment(and_3_out), .input0(i0), .input1(i1),
    .out_7(out_9), .out_8(out_10), .out_9(reg_2bit_1_out_9), .out_10(reg_2bit_1_out_10),
    .out_11(reg_2bit_1_out_11));
  and inc (inc_out, out_10, reg_2bit_1_out_10);
  and dec (dec_out, reg_2bit_1_out_9, reg_2bit_1_out_11);
  and and_4 (and_4_out, and_1_out, in_7);
  and and_5 (and_5_out, and_1_out, not_4_out);
  and and_6 (and_6_out, and_1_out, in_8);
  and inc1 (out_14, out_11, inc_out);
  and dec1 (out_15, j_k_ff_1_qn, dec_out);
  and and_7 (and_7_out, and_1_out, not_5_out);
  or or_1 (or_1_out, and_4_out, dec_out, inc_out);
  or or_2 (or_2_out, clear, inc_out, dec_out, and_5_out);
  or or_3 (or_3_out, and_6_out, out_15, out_14);
  or or_4 (or_4_out, clear, out_14, out_15, and_7_out);
  Clock clock_1 (.out(clock_1_out));
  J_K_Flip_Flop j_k_ff_1 (
    .J(or_1_out), .clk(clock_1_out), .K(or_2_out), .Q(out_11), .Qn(j_k_ff_1_qn));  // open: preset, reset
  J_K_Flip_Flop j_k_ff_2 (
    .J(or_3_out), .clk(clock_1_out), .K(or_4_out), .Q(out_12), .Qn(out_13));  // open: preset, reset

  // Notes on the sheet:
  //   C
  //   L
  //   D
  //   I
  //   input2
  //   input3
  //   2-bit register
  //   L.I2
  //   L.I2'
  //   L.I3
  //   L.I3'
endmodule

module reg_8bit (
  input  clear,
  input  load,
  input  decrement,
  input  in_4,
  input  in_5,
  input  in_6,
  input  in_7,
  input  increment,
  input  in_9,
  input  in_10,
  input  in_11,
  input  in_12,
  output out_13,
  output out_14,
  output out_15,
  output out_16,
  output out_17,
  output out_18,
  output out_19,
  output out_20,
  output out_21,
  output out_22,
  output out_23
);

  wire and_1_out, and_2_out, and_3_out, and_4_out, and_5_out, and_6_out, and_7_out, and_8_out, and_9_out,
       and_10_out, and_11_out, clock_1_out, dec1_out, dec2_out, dec_out, inc1_out, inc2_out, inc_out,
       j_k_ff_1_qn, j_k_ff_2_qn, j_k_ff_3_qn, not_1_out, not_2_out, not_3_out, not_4_out, not_5_out,
       not_6_out, not_7_out, or_1_out, or_2_out, or_3_out, or_4_out, or_5_out, or_6_out, or_7_out, or_8_out,
       reg_4bit_1_out_13, reg_4bit_1_out_14, reg_4bit_1_out_15;

  not not_1 (not_1_out, clear);
  not not_2 (not_2_out, load);
  not not_3 (not_3_out, decrement);
  and and_1 (and_1_out, not_1_out, load);
  and and_2 (and_2_out, not_1_out, not_2_out, decrement);
  and and_3 (and_3_out, not_1_out, not_2_out, not_3_out, increment);
  not not_4 (not_4_out, in_9);
  not not_5 (not_5_out, in_10);
  not not_6 (not_6_out, in_11);
  not not_7 (not_7_out, in_12);
  reg_4bit reg_4bit_1 (
    .clear(clear), .load(and_1_out), .decrement(and_2_out), .increment(and_3_out), .i0(in_4), .i1(in_5),
    .in_7(in_6), .in_8(in_7), .out_9(out_13), .out_10(out_14), .out_11(out_15), .out_12(out_16),
    .out_13(reg_4bit_1_out_13), .out_14(reg_4bit_1_out_14), .out_15(reg_4bit_1_out_15));
  and inc (inc_out, out_16, reg_4bit_1_out_14);
  and dec (dec_out, reg_4bit_1_out_13, reg_4bit_1_out_15);
  and and_4 (and_4_out, and_1_out, in_9);
  and and_5 (and_5_out, and_1_out, not_4_out);
  and and_6 (and_6_out, and_1_out, in_10);
  and inc1 (inc1_out, out_17, inc_out);
  and dec1 (dec1_out, j_k_ff_1_qn, dec_out);
  and and_7 (and_7_out, and_1_out, not_5_out);
  and and_8 (and_8_out, and_1_out, in_11);
  and inc2 (inc2_out, out_18, inc1_out);
  and dec2 (dec2_out, j_k_ff_2_qn, dec1_out);
  and and_9 (and_9_out, and_1_out, not_6_out);
  and and_10 (and_10_out, and_1_out, in_12);
  and inc3 (out_22, out_19, inc2_out);
  and dec3 (out_23, j_k_ff_3_qn, dec2_out);
  and and_11 (and_11_out, and_1_out, not_7_out);
  Clock clock_1 (.out(clock_1_out));
  or or_1 (or_1_out, and_4_out, dec_out, inc_out);
  or or_2 (or_2_out, clear, inc_out, dec_out, and_5_out);
  or or_3 (or_3_out, and_6_out, dec1_out, inc1_out);
  or or_4 (or_4_out, clear, inc1_out, dec1_out, and_7_out);
  or or_5 (or_5_out, and_8_out, dec2_out, inc2_out);
  or or_6 (or_6_out, clear, inc2_out, dec2_out, and_9_out);
  or or_7 (or_7_out, and_10_out, out_23, out_22);
  or or_8 (or_8_out, clear, out_22, out_23, and_11_out);
  J_K_Flip_Flop j_k_ff_1 (
    .J(or_1_out), .clk(clock_1_out), .K(or_2_out), .Q(out_17), .Qn(j_k_ff_1_qn));  // open: preset, reset
  J_K_Flip_Flop j_k_ff_2 (
    .J(or_3_out), .clk(clock_1_out), .K(or_4_out), .Q(out_18), .Qn(j_k_ff_2_qn));  // open: preset, reset
  J_K_Flip_Flop j_k_ff_3 (
    .J(or_5_out), .clk(clock_1_out), .K(or_6_out), .Q(out_19), .Qn(j_k_ff_3_qn));  // open: preset, reset
  J_K_Flip_Flop j_k_ff_4 (
    .J(or_7_out), .clk(clock_1_out), .K(or_8_out), .Q(out_20), .Qn(out_21));  // open: preset, reset

  // Notes on the sheet:
  //   C
  //   L
  //   D
  //   I
  //   i0
  //   i1
  //   i2
  //   i3
  //   input4
  //   input5
  //   input6
  //   input7
  //   4-bit register
  //   L.I4
  //   L.I4'
  //   L.I5
  //   L.I5'
  //   L.I6
  //   L.I6'
  //   L.I7
  //   L.I7'
endmodule

module reg_16bit (
  input  clear,
  input  load,
  input  decrement,
  input  i0,
  input  i1,
  input  i2,
  input  i3,
  input  i4,
  input  i5,
  input  i6,
  input  i7,
  input  increment,
  input  in_13,
  input  input9,
  input  input10,
  input  in_16,
  input  in_17,
  input  input13,
  input  input14,
  input  in_20,
  output out_21,
  output out_22,
  output out_23,
  output out_24,
  output out_25,
  output out_26,
  output out_27,
  output out_28,
  output out_29,
  output out_30,
  output out_31,
  output out_32,
  output out_33,
  output out_34,
  output out_35,
  output out_36
);

  wire and_1_out, and_2_out, and_3_out, and_4_out, and_5_out, and_6_out, and_7_out, and_8_out, and_9_out,
       and_10_out, and_11_out, and_12_out, and_13_out, and_14_out, and_15_out, and_16_out, and_17_out,
       and_18_out, and_19_out, clock_1_out, dec1_out, dec2_out, dec3_out, dec4_out, dec5_out, dec6_out,
       dec7_out, dec_out, inc1_out, inc2_out, inc3_out, inc4_out, inc5_out, inc6_out, inc7_out, inc_out,
       j_k_ff_1_qn, j_k_ff_2_qn, j_k_ff_3_qn, j_k_ff_4_qn, j_k_ff_5_qn, j_k_ff_6_qn, j_k_ff_7_qn, not_1_out,
       not_2_out, not_3_out, not_4_out, not_5_out, not_6_out, not_7_out, not_8_out, not_9_out, not_10_out,
       not_11_out, or_1_out, or_2_out, or_3_out, or_4_out, or_5_out, or_6_out, or_7_out, or_8_out, or_9_out,
       or_10_out, or_11_out, or_12_out, or_13_out, or_14_out, or_15_out, or_16_out, reg_8bit_1_out_21,
       reg_8bit_1_out_22, reg_8bit_1_out_23;

  not not_1 (not_1_out, clear);
  not not_2 (not_2_out, load);
  not not_3 (not_3_out, decrement);
  and and_1 (and_1_out, not_1_out, load);
  and and_2 (and_2_out, not_1_out, not_2_out, decrement);
  and and_3 (and_3_out, not_1_out, not_2_out, not_3_out, increment);
  not not_4 (not_4_out, in_13);
  not not_5 (not_5_out, input9);
  not not_6 (not_6_out, input10);
  not not_7 (not_7_out, in_16);
  not not_8 (not_8_out, in_17);
  not not_9 (not_9_out, input13);
  not not_10 (not_10_out, input14);
  not not_11 (not_11_out, in_20);
  and and_4 (and_4_out, and_1_out, in_13);
  and inc (inc_out, out_28, reg_8bit_1_out_22);
  and dec (dec_out, reg_8bit_1_out_21, reg_8bit_1_out_23);
  and and_5 (and_5_out, and_1_out, not_4_out);
  and and_6 (and_6_out, and_1_out, input9);
  and inc1 (inc1_out, out_29, inc_out);
  and dec1 (dec1_out, j_k_ff_1_qn, dec_out);
  and and_7 (and_7_out, and_1_out, not_5_out);
  and and_8 (and_8_out, and_1_out, input10);
  and inc2 (inc2_out, out_30, inc1_out);
  and dec2 (dec2_out, j_k_ff_2_qn, dec1_out);
  and and_9 (and_9_out, and_1_out, not_6_out);
  and and_10 (and_10_out, and_1_out, in_16);
  and inc3 (inc3_out, out_31, inc2_out);
  and dec3 (dec3_out, j_k_ff_3_qn, dec2_out);
  and and_11 (and_11_out, and_1_out, not_7_out);
  and and_12 (and_12_out, and_1_out, in_17);
  and inc4 (inc4_out, out_32, inc3_out);
  and dec4 (dec4_out, j_k_ff_4_qn, dec3_out);
  and and_13 (and_13_out, and_1_out, not_8_out);
  and and_14 (and_14_out, and_1_out, input13);
  and inc5 (inc5_out, out_33, inc4_out);
  and dec5 (dec5_out, j_k_ff_5_qn, dec4_out);
  and and_15 (and_15_out, and_1_out, not_9_out);
  and and_16 (and_16_out, and_1_out, input14);
  and inc6 (inc6_out, out_34, inc5_out);
  and dec6 (dec6_out, j_k_ff_6_qn, dec5_out);
  and and_17 (and_17_out, and_1_out, not_10_out);
  and and_18 (and_18_out, and_1_out, in_20);
  and inc7 (inc7_out, out_35, inc6_out);
  and dec7 (dec7_out, j_k_ff_7_qn, dec6_out);
  and and_19 (and_19_out, and_1_out, not_11_out);
  reg_8bit reg_8bit_1 (
    .clear(clear), .load(and_1_out), .decrement(and_2_out), .increment(and_3_out), .in_4(i0), .in_5(i1),
    .in_6(i2), .in_7(i3), .in_9(i4), .in_10(i5), .in_11(i6), .in_12(i7), .out_13(out_21), .out_14(out_22),
    .out_15(out_23), .out_16(out_24), .out_17(out_25), .out_18(out_26), .out_19(out_27), .out_20(out_28),
    .out_21(reg_8bit_1_out_21), .out_22(reg_8bit_1_out_22), .out_23(reg_8bit_1_out_23));
  or or_1 (or_1_out, and_4_out, dec_out, inc_out);
  or or_2 (or_2_out, clear, inc_out, dec_out, and_5_out);
  or or_3 (or_3_out, and_6_out, dec1_out, inc1_out);
  or or_4 (or_4_out, clear, inc1_out, dec1_out, and_7_out);
  or or_5 (or_5_out, and_8_out, dec2_out, inc2_out);
  or or_6 (or_6_out, clear, inc2_out, dec2_out, and_9_out);
  or or_7 (or_7_out, and_10_out, dec3_out, inc3_out);
  or or_8 (or_8_out, clear, inc3_out, dec3_out, and_11_out);
  or or_9 (or_9_out, and_12_out, dec4_out, inc4_out);
  or or_10 (or_10_out, clear, inc4_out, dec4_out, and_13_out);
  or or_11 (or_11_out, and_14_out, dec5_out, inc5_out);
  or or_12 (or_12_out, clear, inc5_out, dec5_out, and_15_out);
  or or_13 (or_13_out, and_16_out, dec6_out, inc6_out);
  or or_14 (or_14_out, clear, inc6_out, dec6_out, and_17_out);
  or or_15 (or_15_out, and_18_out, dec7_out, inc7_out);
  or or_16 (or_16_out, clear, inc7_out, dec7_out, and_19_out);
  Clock clock_1 (.out(clock_1_out));
  J_K_Flip_Flop j_k_ff_1 (
    .J(or_1_out), .clk(clock_1_out), .K(or_2_out), .Q(out_29), .Qn(j_k_ff_1_qn));  // open: preset, reset
  J_K_Flip_Flop j_k_ff_2 (
    .J(or_3_out), .clk(clock_1_out), .K(or_4_out), .Q(out_30), .Qn(j_k_ff_2_qn));  // open: preset, reset
  J_K_Flip_Flop j_k_ff_3 (
    .J(or_5_out), .clk(clock_1_out), .K(or_6_out), .Q(out_31), .Qn(j_k_ff_3_qn));  // open: preset, reset
  J_K_Flip_Flop j_k_ff_4 (
    .J(or_7_out), .clk(clock_1_out), .K(or_8_out), .Q(out_32), .Qn(j_k_ff_4_qn));  // open: preset, reset
  J_K_Flip_Flop j_k_ff_5 (
    .J(or_9_out), .clk(clock_1_out), .K(or_10_out), .Q(out_33), .Qn(j_k_ff_5_qn));  // open: preset, reset
  J_K_Flip_Flop j_k_ff_6 (
    .J(or_11_out), .clk(clock_1_out), .K(or_12_out), .Q(out_34), .Qn(j_k_ff_6_qn));  // open: preset, reset
  J_K_Flip_Flop j_k_ff_7 (
    .J(or_13_out), .clk(clock_1_out), .K(or_14_out), .Q(out_35), .Qn(j_k_ff_7_qn));  // open: preset, reset
  J_K_Flip_Flop j_k_ff_8 (.J(or_15_out), .clk(clock_1_out), .K(or_16_out), .Q(out_36));  // open: Qn, preset, reset

  // Notes on the sheet:
  //   C
  //   L
  //   D
  //   I
  //   input8
  //   input11
  //   input12
  //   input15
  //   8-bit register
  //   L.I8
  //   L.I8'
  //   L.I9
  //   L.I9'
  //   L.I10
  //   L.I10'
  //   L.I11
  //   L.I11'
  //   L.I12
  //   L.I12'
  //   L.I13
  //   L.I13'
  //   L.I14
  //   L.I14'
  //   L.I15
  //   L.I15'
endmodule
