// Logisim project 4-bit_computer.circ as structural Verilog: 14 circuits, main circuit main
module main (
  input  T0,
  input  T1,
  input  T2,
  input  T3,
  input  T4,
  input  D0,
  input  D1,
  input  D2,
  input  D3,
  input  D4,
  input  D5,
  input  D6,
  input  D7,
  input  D8,
  input  D9,
  input  D10,
  input  [3:0] INPR,
  input  D11,
  input  D12,
  input  AND_1,
  input  D13,
  input  ADD,
  input  D14,
  input  LD_DR,
  input  D15,
  input  CMA,
  input  CIR,
  input  CIL,
  input  INP,
  output E
);

  wire AC_Manager_ac_bus, AC_Manager_ac_clear, AC_Manager_ac_inc, AC_Manager_ac_load, AR_Manager_ar_bus,
       AR_Manager_ar_inc, AR_Manager_ar_load, clock_1_out, DR_Manager_dr_bus, DR_Manager_dr_load, HLT_hlt,
       IR_Manager_ir_bus, IR_Manager_ir_load, MEM_Manager_memory_bus, MEM_Manager_memory_load,
       OUTR_Manager_outr_load, PC_Manager_pc_bus, PC_Manager_pc_inc, PC_Manager_pc_load;
  wire [3:0] AC_reg_output, ALU_out_13, AR_reg_output, controlled_buffer_1_out, controlled_buffer_1_out_2,
       DR_reg_output, OUTR_reg_output, PC_reg_output;
  wire [7:0] IR_out_5, ram_1_dout;

  HALT HLT (.T3(T3), .D15(D15), .HLT(HLT_hlt));
  Mem_Sub MEM_Manager (
    .T1(T1), .T3(T3), .D0(D0), .D1(D1), .D2(D2), .D3(D3), .D5(D5), .D6(D6),
    .MEMORY_Bus(MEM_Manager_memory_bus), .MEMORY_Load(MEM_Manager_memory_load));
  AR_Sub AR_Manager (
    .T0(T0), .T2(T2), .T3(T3), .T4(T4), .D4(D4), .D5(D5), .AR_Load(AR_Manager_ar_load),
    .AR_Inc(AR_Manager_ar_inc), .AR_Bus(AR_Manager_ar_bus));
  PC_Sub PC_Manager (
    .T0(T0), .T1(T1), .T3(T3), .T4(T4), .D4(D4), .D5(D5), .D6(D6), .PC_Load(PC_Manager_pc_load),
    .PC_Inc(PC_Manager_pc_inc), .PC_Bus(PC_Manager_pc_bus));
  DR_Sub DR_Manager (
    .T3(T3), .T4(T4), .D0(D0), .D1(D1), .D2(D2), .DR_Load(DR_Manager_dr_load), .DR_Bus(DR_Manager_dr_bus));
  AC_Sub AC_Manager (
    .T3(T3), .T4(T4), .D0(D0), .D1(D1), .D2(D2), .D3(D3), .D7(D7), .D9(D9), .D10(D10), .D11(D11), .D12(D12),
    .D13(D13), .D14(D14), .AC_Load(AC_Manager_ac_load), .AC_Inc(AC_Manager_ac_inc),
    .AC_Bus(AC_Manager_ac_bus), .AC_Clear(AC_Manager_ac_clear));
  IR_Sub IR_Manager (.T1(T1), .T2(T2), .IR_Load(IR_Manager_ir_load), .IR_Bus(IR_Manager_ir_bus));
  OUTR_Sub OUTR_Manager (.T3(T3), .D14(D14), .OUTR_Load(OUTR_Manager_outr_load));
  Clock clock_1 (.out(clock_1_out));
  RAM #(.addrWidth(4), .clearpin("true")) ram_1 (
    .addr(AR_reg_output), .we(MEM_Manager_memory_load), .clk(clock_1_out),
    .din({controlled_buffer_1_out_2, controlled_buffer_1_out}), .dout(ram_1_dout), .clr(HLT_hlt));  // open: oe
  ALU_4bit ALU (
    .AC(AC_reg_output), .DR(DR_reg_output), .INPR(INPR), .and_1(AND_1), .add(ADD), .ld_dr(LD_DR), .cma(CMA),
    .cir(CIR), .cil(CIL), .inp(INP), .COUT(E), .out_13(ALU_out_13));  // open: CIN
  Reg_4bit AR (
    .Reg_Input(controlled_buffer_1_out), .Clock(clock_1_out), .Load(AR_Manager_ar_load),
    .Inc(AR_Manager_ar_inc), .Clear(HLT_hlt), .Reg_Output(AR_reg_output));
  Reg_4bit PC (
    .Reg_Input(controlled_buffer_1_out), .Clock(clock_1_out), .Load(PC_Manager_pc_load),
    .Inc(PC_Manager_pc_inc), .Clear(HLT_hlt), .Reg_Output(PC_reg_output));
  Reg_4bit DR (
    .Reg_Input(controlled_buffer_1_out), .Clock(clock_1_out), .Load(DR_Manager_dr_load), .Clear(HLT_hlt),
    .Reg_Output(DR_reg_output));  // open: Inc
  Reg_8bit IR (
    .in_1({controlled_buffer_1_out_2, controlled_buffer_1_out}), .CLK(clock_1_out), .LD(IR_Manager_ir_load),
    .Clear(HLT_hlt), .out_5(IR_out_5));
  // Probe on AR_reg_output
  // Probe on PC_reg_output
  // Probe on DR_reg_output
  // Probe on AC_reg_output
  AC_Reg AC (
    .Reg_Input(ALU_out_13), .Clock(clock_1_out), .Load(AC_Manager_ac_load), .Inc(AC_Manager_ac_inc),
    .Clear(AC_Manager_ac_clear), .Halt(HLT_hlt), .Reg_Output(AC_reg_output));
  // Probe on IR_out_5
  // Probe on OUTR_reg_output
  Reg_4bit OUTR (
    .Reg_Input(controlled_buffer_1_out), .Clock(clock_1_out), .Load(OUTR_Manager_outr_load), .Clear(HLT_hlt),
    .Reg_Output(OUTR_reg_output));  // open: Inc
  assign {controlled_buffer_1_out_2, controlled_buffer_1_out} = MEM_Manager_memory_bus ? ram_1_dout : 8'bz;  // Controlled_Buffer controlled_buffer_1
  assign {controlled_buffer_1_out_2, controlled_buffer_1_out} = AR_Manager_ar_bus ? {4'b0000, AR_reg_output} : 8'bz;  // Controlled_Buffer controlled_buffer_2
  assign {controlled_buffer_1_out_2, controlled_buffer_1_out} = PC_Manager_pc_bus ? {4'b0000, PC_reg_output} : 8'bz;  // Controlled_Buffer controlled_buffer_3
  assign {controlled_buffer_1_out_2, controlled_buffer_1_out} = DR_Manager_dr_bus ? {4'b0000, DR_reg_output} : 8'bz;  // Controlled_Buffer controlled_buffer_4
  assign {controlled_buffer_1_out_2, controlled_buffer_1_out} = AC_Manager_ac_bus ? {4'b0000, AC_reg_output} : 8'bz;  // Controlled_Buffer controlled_buffer_5
  assign {controlled_buffer_1_out_2, controlled_buffer_1_out} = IR_Manager_ir_bus ? IR_out_5 : 8'bz;  // Controlled_Buffer controlled_buffer_6
  // also tied to GND on the sheet: {controlled_buffer_1_out_2[0], controlled_buffer_1_out_2[1], controlled_buffer_1_out_2[2], controlled_buffer_1_out_2[3]}
endmodule

module ALU_1bit (
  input  INPR,
  input  AC,
  input  DR,
  input  and_1,
  input  add_1,
  input  Cin,
  input  Id_DR_1,
  input  cma_1,
  input  cir_1,
  input  cil_1,
  input  ld_inp_1,
  output Cout,
  output out_13
);

  wire ADD_out, adder_1_out, AND1_out, and_1_out, CMA_out, LD_DR_out, LD_INP_out, not_1_out;

  and u_and_1 (and_1_out, DR, AC);
  Adder #(.width(1)) adder_1 (.a(DR), .b(AC), .out(adder_1_out), .cin(Cin), .cout(Cout));
  not not_1 (not_1_out, AC);
  and AND1 (AND1_out, and_1, and_1_out);
  and ADD (ADD_out, add_1, adder_1_out);
  and LD_DR (LD_DR_out, Id_DR_1, DR);
  and CMA (CMA_out, cma_1, not_1_out);
  and LD_INP (LD_INP_out, ld_inp_1, INPR);
  or or_1 (out_13, AND1_out, ADD_out, LD_DR_out, CMA_out, cir_1, cil_1, LD_INP_out);
endmodule

module PC_Sub (
  input  T0,
  input  T1,
  input  T3,
  input  T4,
  input  D4,
  input  D5,
  input  D6,
  output PC_Load,
  output PC_Inc,
  output PC_Bus
);

  wire D4T3_out, D5T3_out, D5T4_out, D6T3_out;

  and D5T4 (D5T4_out, T4, D5);
  and D4T3 (D4T3_out, T3, D4);
  and D6T3 (D6T3_out, T3, D6);
  and D5T3 (D5T3_out, T3, D5);
  or or_1 (PC_Load, D5T4_out, D4T3_out, D6T3_out);
  or or_2 (PC_Bus, D5T3_out, T0);

  assign PC_Inc = T1;

  // Notes on the sheet:
  //   Load = D4T3+D5T4+D6T3
  //   Increment = T1
  //   Bus = T0+D5T3
endmodule

module Reg_4bit (
  input  Inc,
  input  Load,
  input  [3:0] Reg_Input,
  input  Clear,
  input  Clock,
  output [3:0] Reg_Output
);

  wire and_1_out, and_2_out, and_3_out, and_4_out, and_5_out, and_6_out, and_7_out, and_8_out, and_9_out,
       and_10_out, and_11_out, and_12_out, not_1_out, not_2_out, not_3_out, not_4_out, not_5_out, not_6_out,
       or_1_out, or_2_out, or_3_out, or_4_out, or_5_out, or_6_out, or_7_out, or_8_out;

  not not_1 (not_1_out, Load);
  and and_1 (and_1_out, Inc, not_1_out);
  not not_2 (not_2_out, not_1_out);
  not not_3 (not_3_out, Reg_Input[0]);
  not not_4 (not_4_out, Reg_Input[1]);
  not not_5 (not_5_out, Reg_Input[2]);
  not not_6 (not_6_out, Reg_Input[3]);
  and and_2 (and_2_out, not_2_out, Reg_Input[0]);
  and and_3 (and_3_out, not_2_out, not_3_out);
  and and_4 (and_4_out, not_2_out, Reg_Input[1]);
  and and_5 (and_5_out, not_2_out, not_4_out);
  and and_6 (and_6_out, not_2_out, Reg_Input[2]);
  and and_7 (and_7_out, not_2_out, not_5_out);
  and and_8 (and_8_out, not_2_out, Reg_Input[3]);
  and and_9 (and_9_out, not_2_out, not_6_out);
  and and_10 (and_10_out, and_1_out, Reg_Output[0]);
  and and_11 (and_11_out, and_1_out, Reg_Output[0], Reg_Output[1]);
  and and_12 (and_12_out, and_1_out, Reg_Output[0], Reg_Output[1], Reg_Output[2]);
  or or_1 (or_1_out, and_2_out, and_1_out);
  or or_2 (or_2_out, and_3_out, and_1_out);
  or or_3 (or_3_out, and_4_out, and_10_out);
  or or_4 (or_4_out, and_10_out, and_5_out);
  or or_5 (or_5_out, and_6_out, and_11_out);
  or or_6 (or_6_out, and_11_out, and_7_out);
  or or_7 (or_7_out, and_8_out, and_12_out);
  or or_8 (or_8_out, and_12_out, and_9_out);
  J_K_Flip_Flop j_k_ff_1 (
    .J(or_1_out), .clk(Clock), .K(or_2_out), .Q(Reg_Output[0]), .reset(Clear));  // open: Qn, preset
  J_K_Flip_Flop j_k_ff_2 (
    .J(or_3_out), .clk(Clock), .K(or_4_out), .Q(Reg_Output[1]), .reset(Clear));  // open: Qn, preset
  J_K_Flip_Flop j_k_ff_3 (
    .J(or_5_out), .clk(Clock), .K(or_6_out), .Q(Reg_Output[2]), .reset(Clear));  // open: Qn, preset
  J_K_Flip_Flop j_k_ff_4 (
    .J(or_7_out), .clk(Clock), .K(or_8_out), .Q(Reg_Output[3]), .reset(Clear));  // open: Qn, preset
endmodule

module Reg_8bit (
  input  [7:0] in_1,
  input  CLK,
  input  LD,
  input  Clear,
  output [7:0] out_5
);

  // Reg_4bit reg4bit: pin names not known; wires that end beside it: in_1[0], CLK, LD, Clear, out_5[3:0]
  // Reg_4bit reg4bit_2: pin names not known; wires that end beside it: in_1[1], CLK, LD, Clear, out_5[7:4]
  // Pins of 2 and 8 bits meet at in_1
endmodule

module ALU_4bit (
  input  CIN,
  input  [3:0] AC,
  input  [3:0] DR,
  input  [3:0] INPR,
  input  and_1,
  input  add,
  input  ld_dr,
  input  cma,
  input  cir,
  input  cil,
  input  inp,
  output COUT,
  output [3:0] out_13
);

  wire alu_1bit_1_cout, alu_1bit_2_cout, alu_1bit_3_cout;

  ALU_1bit alu_1bit_1 (
    .and_1(and_1), .add_1(add), .Id_DR_1(ld_dr), .cma_1(cma), .cir_1(cir), .cil_1(cil), .ld_inp_1(inp),
    .INPR(INPR[0]), .AC(AC[0]), .DR(DR[0]), .Cin(CIN), .Cout(alu_1bit_1_cout), .out_13(out_13[0]));
  ALU_1bit alu_1bit_2 (
    .and_1(and_1), .add_1(add), .Id_DR_1(ld_dr), .cma_1(cma), .cir_1(cir), .cil_1(cil), .ld_inp_1(inp),
    .INPR(INPR[1]), .AC(AC[1]), .DR(DR[1]), .Cin(alu_1bit_1_cout), .Cout(alu_1bit_2_cout), .out_13(out_13[1]));
  ALU_1bit alu_1bit_3 (
    .and_1(and_1), .add_1(add), .Id_DR_1(ld_dr), .cma_1(cma), .cir_1(cir), .cil_1(cil), .ld_inp_1(inp),
    .INPR(INPR[2]), .AC(AC[2]), .DR(DR[2]), .Cin(alu_1bit_2_cout), .Cout(alu_1bit_3_cout), .out_13(out_13[2]));
  ALU_1bit alu_1bit_4 (
    .and_1(and_1), .add_1(add), .Id_DR_1(ld_dr), .cma_1(cma), .cir_1(cir), .cil_1(cil), .ld_inp_1(inp),
    .INPR(INPR[3]), .AC(AC[3]), .DR(DR[3]), .Cin(alu_1bit_3_cout), .Cout(COUT), .out_13(out_13[3]));
endmodule

module DR_Sub (
  input  T3,
  input  T4,
  input  D0,
  input  D1,
  input  D2,
  output DR_Load,
  output DR_Bus
);

  wire and_1_out, and_2_out, and_3_out;

  and and_1 (and_1_out, T3, D0);
  and and_2 (and_2_out, T3, D2);
  and and_3 (and_3_out, T3, D1);
  or or_1 (DR_Load, and_1_out, and_2_out, and_3_out);
  and and_4 (DR_Bus, T4, D2);

  // Notes on the sheet:
  //   Load = D0T3+D1T3+D2T3
  //   Bus = D2T4
endmodule

module AR_Sub (
  input  T0,
  input  T2,
  input  T3,
  input  T4,
  input  D4,
  input  D5,
  output AR_Load,
  output AR_Inc,
  output AR_Bus
);

  wire and_1_out, and_2_out;

  and and_1 (and_1_out, T3, D4);
  and and_2 (and_2_out, T4, D5);
  or or_1 (AR_Load, T0, T2);
  and and_3 (AR_Inc, T3, D5);
  or or_2 (AR_Bus, and_1_out, and_2_out);

  // Notes on the sheet:
  //   Load = T0+T2
  //   Increment = D5T3
  //   Bus = D5T4+D4T3
endmodule

module AC_Sub (
  input  T3,
  input  T4,
  input  D0,
  input  D1,
  input  D2,
  input  D3,
  input  D7,
  input  D9,
  input  D10,
  input  D11,
  input  D12,
  input  D13,
  input  D14,
  output AC_Load,
  output AC_Inc,
  output AC_Bus,
  output AC_Clear
);

  wire D0T4_out, D1T4_out, D2T4_out, D3T3_out, D9T3_out, D11T3_out, D12T3_out, D13T3_out, D14T3_out;

  and D11T3 (D11T3_out, D11, T3);
  and D9T3 (D9T3_out, T3, D9);
  and D0T4 (D0T4_out, T4, D0);
  and D1T4 (D1T4_out, T4, D1);
  and D2T4 (D2T4_out, T4, D2);
  and D12T3 (D12T3_out, T3, D12);
  and D13T3 (D13T3_out, T3, D13);
  and D10T3 (AC_Inc, T3, D10);
  and D14T3 (D14T3_out, T3, D14);
  and D3T3 (D3T3_out, T3, D3);
  and D7T3 (AC_Clear, T3, D7);
  or LD (AC_Load, D11T3_out, D9T3_out, D0T4_out, D1T4_out, D2T4_out, D12T3_out, D13T3_out);
  or BS (AC_Bus, D14T3_out, D3T3_out);
endmodule

module IR_Sub (
  input  T1,
  input  T2,
  output IR_Load,
  output IR_Bus
);


  assign IR_Bus = T2;
  assign IR_Load = T1;
endmodule

module OUTR_Sub (
  input  T3,
  input  D14,
  output OUTR_Load
);

  and and_1 (OUTR_Load, T3, D14);
endmodule

module Mem_Sub (
  input  T1,
  input  T3,
  input  D0,
  input  D1,
  input  D2,
  input  D3,
  input  D5,
  input  D6,
  output MEMORY_Bus,
  output MEMORY_Load
);

  wire and_1_out, and_2_out, and_3_out, and_4_out, and_5_out, and_6_out;

  and and_1 (and_1_out, T3, D0);
  and and_2 (and_2_out, D1, T3);
  and and_3 (and_3_out, D2, T3);
  and and_4 (and_4_out, D3, T3);
  and and_5 (and_5_out, D5, T3);
  and and_6 (and_6_out, D6, T3);
  or or_1 (MEMORY_Bus, T1, and_1_out, and_2_out, and_3_out, and_6_out);
  or or_2 (MEMORY_Load, and_4_out, and_5_out);
endmodule

module HALT (
  input  T3,
  input  D15,
  output HLT
);

  and and_1 (HLT, T3, D15);
endmodule

module AC_Reg (
  input  Inc,
  input  Load,
  input  [3:0] Reg_Input,
  input  Clock,
  input  Clear,
  input  Halt,
  output [3:0] Reg_Output
);

  wire and_1_out, and_2_out, and_3_out, and_4_out, and_5_out, and_6_out, and_7_out, and_8_out, and_9_out,
       and_10_out, and_11_out, and_12_out, not_1_out, not_2_out, not_3_out, not_4_out, not_5_out, not_6_out,
       or_1_out, or_2_out, or_3_out, or_4_out, or_5_out, or_6_out, or_7_out, or_8_out, or_9_out;

  not not_1 (not_1_out, Load);
  and and_1 (and_1_out, Inc, not_1_out);
  not not_2 (not_2_out, not_1_out);
  not not_3 (not_3_out, Reg_Input[0]);
  not not_4 (not_4_out, Reg_Input[1]);
  not not_5 (not_5_out, Reg_Input[2]);
  not not_6 (not_6_out, Reg_Input[3]);
  and and_2 (and_2_out, not_2_out, Reg_Input[0]);
  and and_3 (and_3_out, not_2_out, not_3_out);
  and and_4 (and_4_out, not_2_out, Reg_Input[1]);
  and and_5 (and_5_out, not_2_out, not_4_out);
  and and_6 (and_6_out, not_2_out, Reg_Input[2]);
  and and_7 (and_7_out, not_2_out, not_5_out);
  and and_8 (and_8_out, not_2_out, Reg_Input[3]);
  and and_9 (and_9_out, not_2_out, not_6_out);
  and and_10 (and_10_out, and_1_out, Reg_Output[0]);
  and and_11 (and_11_out, and_1_out, Reg_Output[0], Reg_Output[1]);
  and and_12 (and_12_out, and_1_out, Reg_Output[0], Reg_Output[1], Reg_Output[2]);
  or or_1 (or_1_out, and_2_out, and_1_out);
  or or_2 (or_2_out, and_3_out, and_1_out);
  or or_3 (or_3_out, and_4_out, and_10_out);
  or or_4 (or_4_out, and_10_out, and_5_out);
  or or_5 (or_5_out, and_6_out, and_11_out);
  or or_6 (or_6_out, and_11_out, and_7_out);
  or or_7 (or_7_out, and_8_out, and_12_out);
  or or_8 (or_8_out, and_12_out, and_9_out);
  J_K_Flip_Flop j_k_ff_1 (
    .J(or_1_out), .clk(Clock), .K(or_2_out), .Q(Reg_Output[0]), .reset(or_9_out));  // open: Qn, preset
  J_K_Flip_Flop j_k_ff_2 (
    .J(or_3_out), .clk(Clock), .K(or_4_out), .Q(Reg_Output[1]), .reset(or_9_out));  // open: Qn, preset
  J_K_Flip_Flop j_k_ff_3 (
    .J(or_5_out), .clk(Clock), .K(or_6_out), .Q(Reg_Output[2]), .reset(or_9_out));  // open: Qn, preset
  J_K_Flip_Flop j_k_ff_4 (
    .J(or_7_out), .clk(Clock), .K(or_8_out), .Q(Reg_Output[3]), .reset(or_9_out));  // open: Qn, preset
  or or_9 (or_9_out, Clear, Halt);
endmodule
