// Logisim project 4-bit_fulladder.circ as structural Verilog: 3 circuits, main circuit main
module main (
  output out_1,
  output out_2,
  output out_3,
  output out_4
);

  wire CLK_out, nand_1_out;

  Clock CLK (.out(CLK_out));
  sub_circuit sub_circuit_1 (.out_1(out_4), .out_2(out_1));
  sub_circuit sub_circuit_2 (.out_1(out_2), .out_2(out_3));
  nand nand_1 (nand_1_out, out_3, out_2);

  // Notes on the sheet:
  //   WEST
  //   SOUTH
  //   EAST
endmodule

// 2-bit sayacı
module sub_circuit (
  output out_1,
  output out_2
);

  wire clock_1_out;

  Clock clock_1 (.out(clock_1_out));
  J_K_Flip_Flop j_k_ff_1 (.J(out_2), .clk(clock_1_out), .K(out_2), .Q(out_1));  // open: Qn, preset, reset
  J_K_Flip_Flop j_k_ff_2 (.J(1'b1), .clk(clock_1_out), .K(1'b1), .Q(out_2));  // open: Qn, preset, reset
endmodule

module asenkron_4bit (
  output _1,
  output _2,
  output _4,
  output _8
);

  wire clock_1_out, j_k_ff_1_q, j_k_ff_2_q, j_k_ff_3_q;

  Clock clock_1 (.out(clock_1_out));
  J_K_Flip_Flop j_k_ff_1 (.J(1'b1), .clk(clock_1_out), .K(1'b1), .Q(j_k_ff_1_q), .Qn(_1));  // open: preset, reset
  J_K_Flip_Flop j_k_ff_2 (.J(1'b1), .clk(j_k_ff_1_q), .K(1'b1), .Q(j_k_ff_2_q), .Qn(_2));  // open: preset, reset
  J_K_Flip_Flop j_k_ff_3 (.J(1'b1), .clk(j_k_ff_2_q), .K(1'b1), .Q(j_k_ff_3_q), .Qn(_4));  // open: preset, reset
  J_K_Flip_Flop j_k_ff_4 (.J(1'b1), .clk(j_k_ff_3_q), .K(1'b1), .Qn(_8));  // open: Q, preset, reset
endmodule
